# Fritzing sketch OLED (saved by Fritzing 0.9.4)

parts:
  OLED1 = 128x64 Monochrom OLED Display with SPI Control
  Part1 = Arduino Uno (Rev3)

nets:
  N1: OLED1.Data, Part1.D11_PWM/MOSI
  N2: OLED1.Clock, Part1.D13/SCK
  N3: OLED1.SA0/DC, Part1.D8
  N4: OLED1.Reset, Part1.D9_PWM
  N5: OLED1.CS, Part1.D10_PWM/SS
  VIN: OLED1.Vin, Part1.5V
  GND: OLED1.GND, Part1.GND
